// Logisim project ProyectoIntegradorTTT.circ as structural Verilog: 5 circuits, main circuit main
module main (
);

  wire _1_out, _2_out, _3_out, _4_out, _5_out, _6_out, _7_out, _8_out, _9_out,
       controlador_entrada_1_bandera_turno, controlador_salida_1_b1, controlador_salida_1_b2,
       controlador_salida_1_b3, controlador_salida_1_b4, controlador_salida_1_b5, controlador_salida_1_b6,
       controlador_salida_1_b7, controlador_salida_1_b8, controlador_salida_1_b9, controlador_salida_1_r1,
       controlador_salida_1_r2, controlador_salida_1_r3, controlador_salida_1_r4, controlador_salida_1_r5,
       controlador_salida_1_r6, controlador_salida_1_r7, controlador_salida_1_r8, controlador_salida_1_r9,
       controlador_salida_1_turno_jugador_2, RESET_out, rgbled_1_p1, rgbled_2_p1, rgbled_2_p2;
  wire [1:0] controlador_entrada_1_boton_1_star, controlador_entrada_1_boton_2_star,
       controlador_entrada_1_boton_3_star, controlador_entrada_1_boton_4_star,
       controlador_entrada_1_boton_5_star, controlador_entrada_1_boton_6_star,
       controlador_entrada_1_boton_7_star, controlador_entrada_1_boton_8_star,
       controlador_entrada_1_boton_9_star, controlador_entrada_1_victoria;

  Button _1 (.out(_1_out));
  Button _4 (.out(_4_out));
  Button _7 (.out(_7_out));
  Button _3 (.out(_3_out));
  Button _2 (.out(_2_out));
  Button _6 (.out(_6_out));
  Button _5 (.out(_5_out));
  Button _9 (.out(_9_out));
  Button _8 (.out(_8_out));
  Controlador_Entrada controlador_entrada_1 (
    .Boton_1(_1_out), .Boton_2(_2_out), .Boton_3(_3_out), .Boton_4(_4_out), .Boton_5(_5_out),
    .Boton_6(_6_out), .Boton_7(_7_out), .Boton_8(_8_out), .Boton_9(_9_out), .Boton_RESET(RESET_out),
    .Bandera_Turno(controlador_entrada_1_bandera_turno), .Boton_1_star(controlador_entrada_1_boton_1_star),
    .Boton_2_star(controlador_entrada_1_boton_2_star), .Boton_3_star(controlador_entrada_1_boton_3_star),
    .Boton_4_star(controlador_entrada_1_boton_4_star), .Boton_5_star(controlador_entrada_1_boton_5_star),
    .Boton_6_star(controlador_entrada_1_boton_6_star), .Boton_7_star(controlador_entrada_1_boton_7_star),
    .Boton_8_star(controlador_entrada_1_boton_8_star), .Boton_9_star(controlador_entrada_1_boton_9_star),
    .Victoria(controlador_entrada_1_victoria));
  // RGBLed rgbled_1: pin names not known; wires that end beside it: rgbled_1_p1, controlador_entrada_1_boton_3_star
  Button RESET (.out(RESET_out));
  // RGBLed rgbled_2: pin names not known; wires that end beside it: rgbled_2_p1, rgbled_2_p2
  Controlador_Salida controlador_salida_1 (
    .Boton_1_star(controlador_entrada_1_boton_1_star), .Boton_2_star(controlador_entrada_1_boton_2_star),
    .Boton_3_star(controlador_entrada_1_boton_3_star), .Boton_4_star(controlador_entrada_1_boton_4_star),
    .Boton_5_star(controlador_entrada_1_boton_5_star), .Boton_6_star(controlador_entrada_1_boton_6_star),
    .Boton_7_star(controlador_entrada_1_boton_7_star), .Boton_8_star(controlador_entrada_1_boton_8_star),
    .Boton_9_star(controlador_entrada_1_boton_9_star), .Bandera_Turno(controlador_entrada_1_bandera_turno),
    .Victoria(controlador_entrada_1_victoria), .R1(controlador_salida_1_r1), .B1(controlador_salida_1_b1),
    .R2(controlador_salida_1_r2), .B2(controlador_salida_1_b2), .R3(controlador_salida_1_r3),
    .B3(controlador_salida_1_b3), .R4(controlador_salida_1_r4), .R5(controlador_salida_1_r5),
    .R6(controlador_salida_1_r6), .B4(controlador_salida_1_b4), .B5(controlador_salida_1_b5),
    .B6(controlador_salida_1_b6), .R7(controlador_salida_1_r7), .R8(controlador_salida_1_r8),
    .R9(controlador_salida_1_r9), .B7(controlador_salida_1_b7), .B8(controlador_salida_1_b8),
    .B9(controlador_salida_1_b9), .Turno_Jugador_1(rgbled_1_p1),
    .Turno_Jugador_2(controlador_salida_1_turno_jugador_2), .BGanador(rgbled_2_p2), .RGanador(rgbled_2_p1));
  // RGBLed rgbled_3: pin names not known; wires that end beside it: controlador_salida_1_turno_jugador_2
  // RGBLed rgbled_4: pin names not known; wires that end beside it: controlador_salida_1_r1, controlador_salida_1_b1
  // RGBLed rgbled_5: pin names not known; wires that end beside it: controlador_salida_1_b3, controlador_salida_1_r4, controlador_salida_1_b4
  // RGBLed rgbled_6: pin names not known; wires that end beside it: controlador_entrada_1_boton_9_star, controlador_salida_1_r7, controlador_salida_1_b7
  // RGBLed rgbled_7: pin names not known; wires that end beside it: controlador_salida_1_r2, controlador_salida_1_b2
  // RGBLed rgbled_8: pin names not known; wires that end beside it: controlador_salida_1_r5, controlador_salida_1_b5
  // RGBLed rgbled_9: pin names not known; wires that end beside it: controlador_salida_1_r8, controlador_salida_1_b8
  // RGBLed rgbled_10: pin names not known; wires that end beside it: controlador_salida_1_r3, controlador_salida_1_b3
  // RGBLed rgbled_11: pin names not known; wires that end beside it: controlador_salida_1_r6, controlador_salida_1_b6
  // RGBLed rgbled_12: pin names not known; wires that end beside it: controlador_salida_1_r9, controlador_salida_1_b9

  // Notes on the sheet:
  //   Proyecto Integrador de Lenguaje Ensamblador$Andrew Rosales Qusada C16971 $Javier Cruz Ruiz C02517 $Jose Amador Mora C10421 
  //   Instrucciones de juego:$-En la parte de la izquierda se encuentran 9 botones, con $estos los jugadores pueden seleccionar la casilla que desean$marcar. $-El turno de cada jugador se decide con los leds de la parte superior,$si el LED del Jugador 1 se enciende, solo se marca la casilla con el$color del Jugador 1, lo mismo para el jugador 2.$-El color del Jugador 1 es azul, y el del jugador 2 es rojo. $-El LED central de la parte superior decide el ganador, este se enciende $en el momento en el que algun jugador gana, y muestra el color del ganador. $-En caso de empate, el LED de "Ganador" se enciende de color morado, la $combinacion de colores de Jugador 1 y Jugador 2. $-En la parte inferior se encuentra un boton llamado "RESET", este se utiliza para$limpiar las casillas y reiniciar el juego. 
  //   Turno Jugador 1
  //   Ganador
  //   Turno Jugador 2
endmodule

module Controlador_Entrada (
  input  Boton_1,
  input  Boton_2,
  input  Boton_3,
  input  Boton_4,
  input  Boton_5,
  input  Boton_6,
  input  Boton_7,
  input  Boton_8,
  input  Boton_9,
  input  Boton_RESET,
  output [1:0] Boton_1_star,
  output [1:0] Boton_2_star,
  output [1:0] Boton_3_star,
  output [1:0] Boton_4_star,
  output [1:0] Boton_5_star,
  output [1:0] Boton_6_star,
  output [1:0] Boton_7_star,
  output [1:0] Boton_8_star,
  output [1:0] Boton_9_star,
  output Bandera_Turno,
  output [1:0] Victoria
);

  wire boton_1_triggered, boton_2_triggered, boton_3_triggered, boton_4_triggered, boton_5_triggered,
       boton_6_triggered, boton_7_triggered, boton_8_triggered, boton_9_triggered, xor_1_out, xor_2_out,
       xor_3_out, xor_4_out, xor_5_out, xor_6_out, xor_7_out;

  Boton u_boton_1 (
    .TRIGGER(Boton_1), .RESET(Boton_RESET), .TURNO(Bandera_Turno), .VALOR(Boton_1_star),
    .TRIGGERED(boton_1_triggered), .VICTORIA(Victoria[0]));
  Boton u_boton_2 (
    .TRIGGER(Boton_2), .RESET(Boton_RESET), .TURNO(Bandera_Turno), .VALOR(Boton_2_star),
    .TRIGGERED(boton_2_triggered), .VICTORIA(Victoria[0]));
  Boton u_boton_3 (
    .TRIGGER(Boton_3), .RESET(Boton_RESET), .TURNO(Bandera_Turno), .VALOR(Boton_3_star),
    .TRIGGERED(boton_3_triggered), .VICTORIA(Victoria[0]));
  Boton u_boton_4 (
    .TRIGGER(Boton_4), .RESET(Boton_RESET), .TURNO(Bandera_Turno), .VALOR(Boton_4_star),
    .TRIGGERED(boton_4_triggered), .VICTORIA(Victoria[0]));
  Boton u_boton_5 (
    .TRIGGER(Boton_5), .RESET(Boton_RESET), .TURNO(Bandera_Turno), .VALOR(Boton_5_star),
    .TRIGGERED(boton_5_triggered), .VICTORIA(Victoria[0]));
  Boton u_boton_6 (
    .TRIGGER(Boton_6), .RESET(Boton_RESET), .TURNO(Bandera_Turno), .VALOR(Boton_6_star),
    .TRIGGERED(boton_6_triggered), .VICTORIA(Victoria[0]));
  Boton u_boton_7 (
    .TRIGGER(Boton_7), .RESET(Boton_RESET), .TURNO(Bandera_Turno), .VALOR(Boton_7_star),
    .TRIGGERED(boton_7_triggered), .VICTORIA(Victoria[0]));
  Boton u_boton_8 (
    .TRIGGER(Boton_8), .RESET(Boton_RESET), .TURNO(Bandera_Turno), .VALOR(Boton_8_star),
    .TRIGGERED(boton_8_triggered), .VICTORIA(Victoria[0]));
  Boton u_boton_9 (
    .TRIGGER(Boton_9), .RESET(Boton_RESET), .TURNO(Bandera_Turno), .VALOR(Boton_9_star),
    .TRIGGERED(boton_9_triggered), .VICTORIA(Victoria[0]));
  xor xor_1 (xor_1_out, boton_1_triggered, boton_2_triggered);
  xor xor_2 (xor_2_out, boton_3_triggered, boton_4_triggered);
  xor xor_3 (xor_3_out, boton_5_triggered, boton_6_triggered);
  xor xor_4 (xor_4_out, boton_7_triggered, boton_8_triggered);
  xor xor_5 (xor_5_out, xor_1_out, xor_2_out);
  xor xor_6 (xor_6_out, xor_3_out, xor_4_out);
  xor xor_7 (xor_7_out, xor_5_out, xor_6_out);
  xor xor_8 (Bandera_Turno, xor_7_out, boton_9_triggered);
  Condiciones_de_Victoria condiciones_de_victoria_1 (
    .Boton_1_star(Boton_1_star), .Boton_2_star(Boton_2_star), .Boton_3_star(Boton_3_star),
    .Victoria(Victoria), .Boton_4_star(Boton_4_star), .Boton_5_star(Boton_5_star),
    .Boton_6_star(Boton_6_star), .Boton_7_star(Boton_7_star), .Boton_8_star(Boton_8_star),
    .Boton_9_star(Boton_9_star));

  // Notes on the sheet:
  //   Entrada
  //   Salida
endmodule

module Controlador_Salida (
  input  [1:0] Boton_1_star,
  input  [1:0] Boton_2_star,
  input  [1:0] Boton_3_star,
  input  [1:0] Boton_4_star,
  input  [1:0] Boton_5_star,
  input  [1:0] Boton_6_star,
  input  [1:0] Boton_7_star,
  input  [1:0] Boton_8_star,
  input  [1:0] Boton_9_star,
  input  Bandera_Turno,
  input  [1:0] Victoria,
  output R1,
  output R2,
  output R3,
  output B1,
  output B2,
  output B3,
  output R4,
  output R5,
  output R6,
  output B4,
  output B5,
  output B6,
  output R7,
  output R8,
  output R9,
  output B7,
  output B8,
  output B9,
  output Turno_Jugador_1,
  output Turno_Jugador_2,
  output BGanador,
  output RGanador
);

  wire comparator_1_eq, comparator_2_eq, not_1_out;
  wire [1:0] multiplexer_2_out;

  Comparator #(.width(2), .mode("unsigned")) comparator_1 (
    .a(Victoria), .b(2'b00), .eq(comparator_1_eq));  // open: gt, lt
  not not_1 (not_1_out, Bandera_Turno);
  Multiplexer #(.enable("false")) multiplexer_1 (
    .in0(not_1_out), .in1(Bandera_Turno), .out(Turno_Jugador_2), .sel(comparator_1_eq));
  not not_2 (Turno_Jugador_1, Turno_Jugador_2);
  Multiplexer #(.width(2), .enable("false")) multiplexer_2 (
    .in0({Turno_Jugador_2, Turno_Jugador_1}), .in1(2'b00), .out(multiplexer_2_out), .sel(comparator_1_eq));
  Comparator #(.width(2), .mode("unsigned")) comparator_2 (
    .a(Victoria), .b(2'b10), .eq(comparator_2_eq));  // open: gt, lt
  Multiplexer #(.width(2), .enable("false")) multiplexer_3 (
    .in0(multiplexer_2_out), .in1(2'b11), .out({RGanador, BGanador}), .sel(comparator_2_eq));

  assign B1 = Boton_1_star[0];
  assign B2 = Boton_2_star[0];
  assign B3 = Boton_3_star[0];
  assign B4 = Boton_4_star[0];
  assign B5 = Boton_5_star[0];
  assign B6 = Boton_6_star[0];
  assign B7 = Boton_7_star[0];
  assign B8 = Boton_8_star[0];
  assign B9 = Boton_9_star[0];
  assign R1 = Boton_1_star[1];
  assign R2 = Boton_2_star[1];
  assign R3 = Boton_3_star[1];
  assign R4 = Boton_4_star[1];
  assign R5 = Boton_5_star[1];
  assign R6 = Boton_6_star[1];
  assign R7 = Boton_7_star[1];
  assign R8 = Boton_8_star[1];
  assign R9 = Boton_9_star[1];

  // Notes on the sheet:
  //   Entrada
  //   Leds Botones
  //   Salida
  //   Leds Turnos y Ganador
endmodule

module Boton (
  input  TRIGGER,
  input  RESET,
  input  TURNO,
  input  VICTORIA,
  output [1:0] VALOR,
  output TRIGGERED
);

  wire d_ff_2_q, d_ff_3_q, demultiplexer_1_out1, multiplexer_1_out, not_1_out, or_1_out;
  wire [0:0] demultiplexer_1_out0;
  wire [1:0] multiplexer_3_out;

  Multiplexer #(.enable("false")) multiplexer_1 (.in0(TRIGGER), .in1(1'b0), .out(multiplexer_1_out), .sel(VICTORIA));
  D_Flip_Flop d_ff_1 (
    .clk(multiplexer_1_out), .D(multiplexer_1_out), .Q(TRIGGERED), .reset(RESET));  // open: Qn, preset
  not not_1 (not_1_out, TURNO);
  D_Flip_Flop d_ff_2 (.clk(TRIGGERED), .D(not_1_out), .Q(d_ff_2_q), .reset(RESET));  // open: Qn, preset
  D_Flip_Flop d_ff_3 (.clk(TRIGGERED), .D(TURNO), .Q(d_ff_3_q), .reset(RESET));  // open: Qn, preset
  Demultiplexer #(.enable("false")) demultiplexer_1 (
    .out0(demultiplexer_1_out0[0]), .out1(demultiplexer_1_out1), .in(d_ff_2_q), .sel(or_1_out));
  or or_1 (or_1_out, d_ff_2_q, d_ff_3_q);
  Multiplexer #(.width(2), .enable("false")) multiplexer_2 (
    .in0({1'b0, demultiplexer_1_out0[0]}), .in1(multiplexer_3_out), .out(VALOR), .sel(or_1_out));
  Multiplexer #(.width(2), .enable("false")) multiplexer_3 (
    .in0(2'b10), .in1(2'b01), .out(multiplexer_3_out), .sel(demultiplexer_1_out1));

  // Notes on the sheet:
  //   Entrada
  //   Salida
endmodule

module Condiciones_de_Victoria (
  input  [1:0] Boton_1_star,
  input  [1:0] Boton_2_star,
  input  [1:0] Boton_3_star,
  input  [1:0] Boton_4_star,
  input  [1:0] Boton_5_star,
  input  [1:0] Boton_6_star,
  input  [1:0] Boton_7_star,
  input  [1:0] Boton_8_star,
  input  [1:0] Boton_9_star,
  output [1:0] Victoria
);

  wire and_1_out, and_2_out, and_3_out, and_5_out, and_6_out, and_7_out, and_8_out, and_9_out,
       comparator_1_eq, comparator_2_eq, comparator_3_eq, comparator_4_eq, comparator_5_eq, comparator_6_eq,
       comparator_7_eq, comparator_8_eq, comparator_9_eq, comparator_10_eq, comparator_11_eq,
       comparator_12_eq, comparator_13_eq, comparator_14_eq, comparator_15_eq, comparator_16_eq,
       comparator_17_eq, comparator_18_eq, comparator_19_eq, comparator_20_eq, comparator_21_eq,
       comparator_22_eq, comparator_23_eq, comparator_24_eq, comparator_25_eq, comparator_26_eq,
       comparator_27_eq, comparator_28_eq, comparator_29_eq, comparator_30_eq, comparator_31_eq,
       comparator_32_eq, not_1_out, not_2_out, not_3_out, not_4_out, not_5_out, not_6_out, not_7_out,
       not_8_out, not_9_out, not_10_out, not_11_out, not_12_out, not_13_out, not_14_out, not_15_out,
       not_16_out, or_1_out, Posible_Empate, Victoria_Diagonal, Victoria_Horizontal, Victoria_Vertical;
  wire [1:0] multiplexer_1_out;

  Comparator #(.width(2), .mode("unsigned")) comparator_1 (
    .a(Boton_1_star), .b(2'b00), .eq(comparator_1_eq));  // open: gt, lt
  not not_1 (not_1_out, comparator_1_eq);
  Comparator #(.width(2), .mode("unsigned")) comparator_2 (
    .a(Boton_1_star), .b(Boton_2_star), .eq(comparator_2_eq));  // open: gt, lt
  Comparator #(.width(2), .mode("unsigned")) comparator_3 (
    .a(Boton_1_star), .b(Boton_3_star), .eq(comparator_3_eq));  // open: gt, lt
  Comparator #(.width(2), .mode("unsigned")) comparator_4 (
    .a(Boton_4_star), .b(2'b00), .eq(comparator_4_eq));  // open: gt, lt
  not not_2 (not_2_out, comparator_4_eq);
  Comparator #(.width(2), .mode("unsigned")) comparator_5 (
    .a(Boton_4_star), .b(Boton_5_star), .eq(comparator_5_eq));  // open: gt, lt
  Comparator #(.width(2), .mode("unsigned")) comparator_6 (
    .a(Boton_4_star), .b(Boton_6_star), .eq(comparator_6_eq));  // open: gt, lt
  not not_3 (not_3_out, comparator_7_eq);
  Comparator #(.width(2), .mode("unsigned")) comparator_7 (
    .a(Boton_7_star), .b(2'b00), .eq(comparator_7_eq));  // open: gt, lt
  Comparator #(.width(2), .mode("unsigned")) comparator_8 (
    .a(Boton_7_star), .b(Boton_8_star), .eq(comparator_8_eq));  // open: gt, lt
  Comparator #(.width(2), .mode("unsigned")) comparator_9 (
    .a(Boton_7_star), .b(Boton_9_star), .eq(comparator_9_eq));  // open: gt, lt
  not not_4 (not_4_out, comparator_10_eq);
  Comparator #(.width(2), .mode("unsigned")) comparator_10 (
    .a(Boton_1_star), .b(2'b00), .eq(comparator_10_eq));  // open: gt, lt
  not not_5 (not_5_out, comparator_11_eq);
  Comparator #(.width(2), .mode("unsigned")) comparator_11 (
    .a(Boton_2_star), .b(2'b00), .eq(comparator_11_eq));  // open: gt, lt
  Comparator #(.width(2), .mode("unsigned")) comparator_12 (
    .a(Boton_3_star), .b(2'b00), .eq(comparator_12_eq));  // open: gt, lt
  not not_6 (not_6_out, comparator_12_eq);
  Comparator #(.width(2), .mode("unsigned")) comparator_13 (
    .a(Boton_4_star), .b(2'b00), .eq(comparator_13_eq));  // open: gt, lt
  not not_7 (not_7_out, comparator_13_eq);
  not not_8 (not_8_out, comparator_14_eq);
  Comparator #(.width(2), .mode("unsigned")) comparator_14 (
    .a(Boton_5_star), .b(2'b00), .eq(comparator_14_eq));  // open: gt, lt
  Comparator #(.width(2), .mode("unsigned")) comparator_15 (
    .a(Boton_6_star), .b(2'b00), .eq(comparator_15_eq));  // open: gt, lt
  not not_9 (not_9_out, comparator_15_eq);
  not not_10 (not_10_out, comparator_16_eq);
  Comparator #(.width(2), .mode("unsigned")) comparator_16 (
    .a(Boton_7_star), .b(2'b00), .eq(comparator_16_eq));  // open: gt, lt
  Comparator #(.width(2), .mode("unsigned")) comparator_17 (
    .a(Boton_8_star), .b(2'b00), .eq(comparator_17_eq));  // open: gt, lt
  not not_11 (not_11_out, comparator_17_eq);
  not not_12 (not_12_out, comparator_18_eq);
  Comparator #(.width(2), .mode("unsigned")) comparator_18 (
    .a(Boton_9_star), .b(2'b00), .eq(comparator_18_eq));  // open: gt, lt
  or or_1 (or_1_out, Victoria_Horizontal, Victoria_Diagonal, Victoria_Vertical);
  and and_1 (and_1_out, not_1_out, comparator_2_eq, comparator_3_eq);
  and and_2 (and_2_out, not_2_out, comparator_5_eq, comparator_6_eq);
  and and_3 (and_3_out, not_3_out, comparator_8_eq, comparator_9_eq);
  and and_4 (Posible_Empate, not_4_out, not_5_out, not_6_out, not_7_out, not_8_out, not_9_out, not_10_out, not_11_out, not_12_out);
  Multiplexer #(.width(2), .enable("false")) multiplexer_1 (
    .in0(2'b00), .in1(2'b10), .out(multiplexer_1_out), .sel(Posible_Empate));
  Multiplexer #(.width(2), .enable("false")) multiplexer_2 (
    .in0(multiplexer_1_out), .in1(2'b01), .out(Victoria), .sel(or_1_out));
  or or_2 (Victoria_Horizontal, and_1_out, and_2_out, and_3_out);
  not not_13 (not_13_out, comparator_19_eq);
  Comparator #(.width(2), .mode("unsigned")) comparator_19 (
    .a(Boton_1_star), .b(2'b00), .eq(comparator_19_eq));  // open: gt, lt
  Comparator #(.width(2), .mode("unsigned")) comparator_20 (
    .a(Boton_1_star), .b(Boton_4_star), .eq(comparator_20_eq));  // open: gt, lt
  Comparator #(.width(2), .mode("unsigned")) comparator_21 (
    .a(Boton_1_star), .b(Boton_7_star), .eq(comparator_21_eq));  // open: gt, lt
  not not_14 (not_14_out, comparator_22_eq);
  Comparator #(.width(2), .mode("unsigned")) comparator_22 (
    .a(Boton_2_star), .b(2'b00), .eq(comparator_22_eq));  // open: gt, lt
  Comparator #(.width(2), .mode("unsigned")) comparator_23 (
    .a(Boton_2_star), .b(Boton_5_star), .eq(comparator_23_eq));  // open: gt, lt
  Comparator #(.width(2), .mode("unsigned")) comparator_24 (
    .a(Boton_2_star), .b(Boton_8_star), .eq(comparator_24_eq));  // open: gt, lt
  not not_15 (not_15_out, comparator_25_eq);
  Comparator #(.width(2), .mode("unsigned")) comparator_25 (
    .a(Boton_3_star), .b(2'b00), .eq(comparator_25_eq));  // open: gt, lt
  Comparator #(.width(2), .mode("unsigned")) comparator_26 (
    .a(Boton_3_star), .b(Boton_6_star), .eq(comparator_26_eq));  // open: gt, lt
  Comparator #(.width(2), .mode("unsigned")) comparator_27 (
    .a(Boton_3_star), .b(Boton_9_star), .eq(comparator_27_eq));  // open: gt, lt
  Comparator #(.width(2), .mode("unsigned")) comparator_28 (
    .a(Boton_5_star), .b(2'b00), .eq(comparator_28_eq));  // open: gt, lt
  not not_16 (not_16_out, comparator_28_eq);
  Comparator #(.width(2), .mode("unsigned")) comparator_29 (
    .a(Boton_5_star), .b(Boton_1_star), .eq(comparator_29_eq));  // open: gt, lt
  Comparator #(.width(2), .mode("unsigned")) comparator_30 (
    .a(Boton_5_star), .b(Boton_9_star), .eq(comparator_30_eq));  // open: gt, lt
  Comparator #(.width(2), .mode("unsigned")) comparator_31 (
    .a(Boton_5_star), .b(Boton_3_star), .eq(comparator_31_eq));  // open: gt, lt
  Comparator #(.width(2), .mode("unsigned")) comparator_32 (
    .a(Boton_5_star), .b(Boton_7_star), .eq(comparator_32_eq));  // open: gt, lt
  and and_5 (and_5_out, not_13_out, comparator_20_eq, comparator_21_eq);
  and and_6 (and_6_out, not_14_out, comparator_23_eq, comparator_24_eq);
  and and_7 (and_7_out, not_15_out, comparator_26_eq, comparator_27_eq);
  and and_8 (and_8_out, not_16_out, comparator_29_eq, comparator_30_eq);
  and and_9 (and_9_out, not_16_out, comparator_31_eq, comparator_32_eq);
  or or_3 (Victoria_Vertical, and_5_out, and_6_out, and_7_out);
  or or_4 (Victoria_Diagonal, and_8_out, and_9_out);

  // Notes on the sheet:
  //   Entrada
  //   Condiciones de Victoria Horizontales
  //   Condicion de Empate
  //   Resultado Final
  //   Salida
  //   Condiciones de Victoria Verticales
  //   Condiciones de Victoria Diagonales
endmodule
