// Logisim project Tic tac toe.circ as structural Verilog: 2 circuits, main circuit Tablero
module Tablero (
);

  wire _1_p2, _2_p2, _3_p2, _4_p2, _5_p2, _6_p2, _7_p2, _8_p2, _9_p2, circuitoganador_1_ganador;

  LED led_1 (.in(_1_p2));
  LED led_2 (.in(_4_p2));
  LED led_3 (.in(_7_p2));
  LED led_4 (.in(_2_p2));
  LED led_5 (.in(_5_p2));
  LED led_6 (.in(_8_p2));
  LED led_7 (.in(_3_p2));
  LED led_8 (.in(_6_p2));
  LED led_9 (.in(_9_p2));
  // Switch _1: pin names not known; wires that end beside it: 1'b1, _1_p2
  // Switch _2: pin names not known; wires that end beside it: 1'b1, _2_p2
  // Switch _4: pin names not known; wires that end beside it: 1'b1, _4_p2
  // Switch _5: pin names not known; wires that end beside it: 1'b1, _5_p2
  // Switch _7: pin names not known; wires that end beside it: 1'b1, _7_p2
  // Switch _8: pin names not known; wires that end beside it: 1'b1, _8_p2
  // Switch _3: pin names not known; wires that end beside it: 1'b1, _3_p2
  // Switch _6: pin names not known; wires that end beside it: 1'b1, _6_p2
  // Switch _9: pin names not known; wires that end beside it: 1'b1, _9_p2
  CircuitoGanador circuitoganador_1 (
    .Boton3(_3_p2), .Ganador(circuitoganador_1_ganador), .Boton2(_2_p2), .Boton1(_1_p2), .Boton6(_6_p2),
    .Boton5(_5_p2), .Boton4(_4_p2), .Boton9(_9_p2), .Boton8(_8_p2), .Boton7(_7_p2));
  LED Ganador (.in(circuitoganador_1_ganador));

  // Notes on the sheet:
  //   Acá hice un diseño rapido del teclado, nada mas para ver que funciona$el circuito que determina el ganador, faltaría determinar los turnos, hay que ponerle$dos leds a cada casilla en lugar de uno y dependiendo de cual turno sea se enciende $cierto LED
endmodule

module CircuitoGanador (
  input  Boton3,
  input  Boton2,
  input  Boton1,
  input  Boton6,
  input  Boton5,
  input  Boton4,
  input  Boton9,
  input  Boton8,
  input  Boton7,
  output Ganador
);

  wire and_1_out, and_2_out, and_3_out, and_4_out, and_5_out, and_6_out, and_7_out, and_8_out, or_1_out,
       or_2_out;

  and and_1 (and_1_out, Boton3, Boton2, Boton1);
  and and_2 (and_2_out, Boton6, Boton5, Boton4);
  and and_3 (and_3_out, Boton9, Boton8, Boton7);
  and and_4 (and_4_out, Boton1, Boton4, Boton7);
  and and_5 (and_5_out, Boton2, Boton5, Boton8);
  and and_6 (and_6_out, Boton3, Boton6, Boton9);
  and and_7 (and_7_out, Boton1, Boton5, Boton9);
  and and_8 (and_8_out, Boton3, Boton5, Boton7);
  or or_1 (or_1_out, and_1_out, and_2_out, and_3_out, and_4_out);
  or or_2 (or_2_out, and_5_out, and_6_out, and_7_out, and_8_out);
  or or_3 (Ganador, or_1_out, or_2_out);

  // Notes on the sheet:
  //   Entradas
  //   Salidas
endmodule
